// Logisim project uart_rx_log.circ as structural Verilog
module main (
  input  run_test,
  input  serial_in,
  output bit_out,
  output [7:0] letter_0,
  output [7:0] letter_1,
  output [7:0] letter_2,
  output [7:0] letter_3,
  output [7:0] letter_4,
  output [7:0] letter_5
);

  wire clock_1_out, uart_rx_1_o_rx_dv, uart_tx_1_busy, uart_tx_tester_1_trigger;
  wire [7:0] bin_to_letter_1_display_letter, uart_rx_1_o_rx_byte, uart_tx_tester_1_data_out;

  Clock clock_1 (.out(clock_1_out));
  uart_tx_tester uart_tx_tester_1 (
    .clk_50M(clock_1_out), .run_test_raw(run_test), .tx_busy(uart_tx_1_busy),
    .data_out(uart_tx_tester_1_data_out), .trigger(uart_tx_tester_1_trigger));
  uart_rx uart_rx_1 (
    .i_Clock(clock_1_out), .i_RX_Serial(serial_in), .o_RX_DV(uart_rx_1_o_rx_dv),
    .o_RX_Byte(uart_rx_1_o_rx_byte));  // open: o_Start_Done, o_FSM_Mode, o_Bit_Index
  bin_to_letter bin_to_letter_1 (.input_letter(uart_rx_1_o_rx_byte), .display_letter(bin_to_letter_1_display_letter));
  uart_tx uart_tx_1 (
    .clk_50M(clock_1_out), .data_raw(uart_tx_tester_1_data_out), .trigger_raw(uart_tx_tester_1_trigger),
    .busy(uart_tx_1_busy), .serial_out(bit_out));  // open: tx_index_out
  sentence_disp sentence_disp_1 (
    .new_letter(bin_to_letter_1_display_letter), .update(uart_rx_1_o_rx_dv), .seg0(letter_0),
    .seg1(letter_1), .seg2(letter_2), .seg3(letter_3), .seg4(letter_4), .seg5(letter_5));
endmodule

module bin_to_letter (
  input  [7:0] input_letter,
  output [7:0] display_letter
);

  wire and_1_out, and_2_out, and_3_out, and_4_out, and_5_out, and_6_out, and_7_out, and_8_out, and_9_out,
       and_10_out, and_11_out, and_12_out, and_13_out, and_14_out, and_15_out, and_16_out, and_17_out,
       and_18_out, and_19_out, and_20_out, and_21_out, and_22_out, and_23_out, and_24_out, and_25_out,
       and_26_out, and_27_out, and_28_out, and_29_out, and_30_out, and_31_out, and_32_out, and_33_out,
       and_34_out, and_35_out, and_36_out, and_37_out, and_38_out, and_39_out, and_40_out, and_41_out,
       and_42_out, and_43_out, and_44_out, and_45_out, and_46_out, and_47_out, and_48_out, and_49_out,
       and_50_out, and_51_out, and_52_out, and_53_out, and_54_out, and_55_out, and_56_out, and_57_out,
       and_58_out, and_59_out, and_60_out, and_61_out, and_62_out, and_63_out, and_64_out, and_65_out,
       and_66_out, and_67_out, and_68_out, and_69_out, and_70_out, and_71_out, and_72_out, and_73_out,
       and_74_out, and_75_out, not_1_out, not_2_out, not_3_out, not_4_out, not_5_out, not_6_out, not_7_out,
       not_8_out;

  not not_1 (not_1_out, input_letter[7]);
  not not_2 (not_2_out, input_letter[6]);
  not not_3 (not_3_out, input_letter[5]);
  not not_4 (not_4_out, input_letter[4]);
  not not_5 (not_5_out, input_letter[3]);
  not not_6 (not_6_out, input_letter[2]);
  not not_7 (not_7_out, input_letter[1]);
  not not_8 (not_8_out, input_letter[0]);
  and and_1 (and_1_out, not_1_out, not_2_out, not_3_out, not_4_out, not_5_out, not_6_out, not_7_out, not_8_out);
  and and_2 (and_2_out, not_1_out, input_letter[6], not_4_out, input_letter[3], not_6_out, input_letter[1], input_letter[0]);
  and and_3 (and_3_out, input_letter[7], input_letter[6], input_letter[5], input_letter[4], input_letter[3], input_letter[2], input_letter[1], input_letter[0]);
  and and_4 (and_4_out, not_1_out, input_letter[6], not_4_out, not_5_out, not_7_out, input_letter[0]);
  and and_5 (and_5_out, not_1_out, input_letter[6], not_4_out, not_5_out, input_letter[1], not_8_out);
  and and_6 (and_6_out, not_1_out, input_letter[6], not_5_out, input_letter[2], not_7_out, not_8_out);
  and and_7 (and_7_out, not_1_out, input_letter[6], not_4_out, input_letter[2], input_letter[1], not_8_out);
  and and_8 (and_8_out, not_1_out, input_letter[6], not_4_out, input_letter[3], not_6_out, not_7_out, not_8_out);
  and and_9 (and_9_out, not_1_out, input_letter[6], not_4_out, input_letter[3], not_6_out, input_letter[1], input_letter[0]);
  and and_10 (and_10_out, not_1_out, input_letter[6], input_letter[4], not_5_out, not_6_out);
  and and_11 (and_11_out, not_1_out, input_letter[6], input_letter[4], not_6_out, not_7_out, input_letter[0]);
  and and_12 (and_12_out, not_1_out, input_letter[6], input_letter[4], not_6_out, input_letter[1], not_8_out);
  and and_13 (and_13_out, not_1_out, input_letter[6], input_letter[5], not_5_out, not_6_out, input_letter[0]);
  and and_14 (and_14_out, not_1_out, input_letter[6], input_letter[5], not_4_out, input_letter[1], input_letter[0]);
  and and_15 (and_15_out, input_letter[7], input_letter[6], input_letter[5], input_letter[4], input_letter[3], input_letter[2], input_letter[1], input_letter[0]);
  and and_16 (and_16_out, not_1_out, input_letter[6], not_5_out, not_7_out, input_letter[0]);
  and and_17 (and_17_out, not_1_out, input_letter[6], not_3_out, not_4_out, not_5_out, input_letter[1]);
  and and_18 (and_18_out, not_1_out, input_letter[6], not_4_out, not_5_out, input_letter[1], not_8_out);
  and and_19 (and_19_out, not_1_out, input_letter[6], not_3_out, not_4_out, input_letter[2], input_letter[0]);
  and and_20 (and_20_out, not_1_out, input_letter[6], not_4_out, not_5_out, input_letter[2], input_letter[1]);
  and and_21 (and_21_out, not_1_out, input_letter[6], not_4_out, input_letter[3], not_7_out, not_8_out);
  and and_22 (and_22_out, not_1_out, input_letter[6], not_4_out, input_letter[3], not_6_out, input_letter[1], input_letter[0]);
  and and_23 (and_23_out, not_1_out, input_letter[6], not_4_out, input_letter[3], input_letter[2], not_7_out);
  and and_24 (and_24_out, not_1_out, input_letter[6], input_letter[4], not_5_out, not_7_out);
  and and_25 (and_25_out, not_1_out, input_letter[6], input_letter[4], not_6_out, not_7_out);
  and and_26 (and_26_out, not_1_out, input_letter[6], input_letter[4], not_5_out, not_6_out, input_letter[0]);
  and and_27 (and_27_out, input_letter[7], input_letter[6], input_letter[5], input_letter[4], input_letter[3], input_letter[2], input_letter[1], input_letter[0]);
  and and_28 (and_28_out, not_1_out, input_letter[6], not_3_out, not_4_out, input_letter[0]);
  and and_29 (and_29_out, not_1_out, input_letter[6], not_4_out, not_6_out, input_letter[0]);
  and and_30 (and_30_out, not_1_out, input_letter[6], not_5_out, input_letter[1], not_8_out);
  and and_31 (and_31_out, not_1_out, input_letter[6], not_5_out, input_letter[2], not_7_out);
  and and_32 (and_32_out, not_1_out, input_letter[6], not_4_out, input_letter[3], not_7_out);
  and and_33 (and_33_out, not_1_out, input_letter[6], not_4_out, input_letter[3], input_letter[2]);
  and and_34 (and_34_out, not_1_out, input_letter[6], input_letter[4], not_6_out, not_8_out);
  and and_35 (and_35_out, not_1_out, input_letter[6], input_letter[4], not_5_out, input_letter[2]);
  and and_36 (and_36_out, input_letter[7], input_letter[6], input_letter[5], input_letter[4], input_letter[3], input_letter[2], input_letter[1], input_letter[0]);
  and and_37 (and_37_out, not_1_out, input_letter[6], not_4_out, not_5_out, not_6_out, input_letter[1]);
  and and_38 (and_38_out, not_1_out, input_letter[6], not_5_out, input_letter[1], input_letter[0]);
  and and_39 (and_39_out, not_1_out, input_letter[6], not_3_out, not_4_out, input_letter[2], not_7_out, not_8_out);
  and and_40 (and_40_out, not_1_out, input_letter[6], not_4_out, not_5_out, input_letter[2], not_7_out);
  and and_41 (and_41_out, not_1_out, input_letter[6], not_5_out, input_letter[2], input_letter[0]);
  and and_42 (and_42_out, not_1_out, input_letter[6], not_4_out, input_letter[2], input_letter[1], input_letter[0]);
  and and_43 (and_43_out, not_1_out, input_letter[6], input_letter[3], not_6_out, input_letter[1], not_8_out);
  and and_44 (and_44_out, input_letter[7], input_letter[6], input_letter[5], input_letter[4], input_letter[3], input_letter[2], input_letter[1], input_letter[0]);
  and and_45 (and_45_out, not_1_out, input_letter[6], not_5_out, not_6_out, not_7_out, input_letter[0]);
  and and_46 (and_46_out, not_1_out, input_letter[6], not_4_out, not_6_out, input_letter[1], not_8_out);
  and and_47 (and_47_out, not_1_out, input_letter[6], not_4_out, not_5_out, input_letter[2], not_7_out, not_8_out);
  and and_48 (and_48_out, not_1_out, input_letter[6], not_4_out, input_letter[2], input_letter[1], input_letter[0]);
  and and_49 (and_49_out, not_1_out, input_letter[6], input_letter[3], not_6_out, not_7_out, not_8_out);
  and and_50 (and_50_out, not_1_out, input_letter[6], not_4_out, input_letter[3], input_letter[1], not_8_out);
  and and_51 (and_51_out, not_1_out, input_letter[6], not_4_out, input_letter[3], input_letter[2], input_letter[0]);
  and and_52 (and_52_out, not_1_out, input_letter[6], input_letter[4], not_5_out, input_letter[0]);
  and and_53 (and_53_out, not_1_out, input_letter[6], input_letter[4], not_5_out, input_letter[2], input_letter[1]);
  and and_54 (and_54_out, not_1_out, input_letter[6], input_letter[4], input_letter[3], not_6_out, not_7_out);
  and and_55 (and_55_out, input_letter[7], input_letter[6], input_letter[5], input_letter[4], input_letter[3], input_letter[2], input_letter[1], input_letter[0]);
  and and_56 (and_56_out, not_1_out, input_letter[6], not_5_out, not_6_out, not_7_out, input_letter[0]);
  and and_57 (and_57_out, not_1_out, input_letter[6], not_4_out, not_5_out, input_letter[2], not_7_out, not_8_out);
  and and_58 (and_58_out, not_1_out, input_letter[6], not_3_out, input_letter[3], not_6_out, not_8_out);
  and and_59 (and_59_out, not_1_out, input_letter[6], not_4_out, input_letter[3], not_6_out, input_letter[1]);
  and and_60 (and_60_out, not_1_out, input_letter[6], not_3_out, not_4_out, input_letter[3], input_letter[2], input_letter[0]);
  and and_61 (and_61_out, not_1_out, input_letter[6], not_4_out, input_letter[3], input_letter[2], not_7_out, input_letter[0]);
  and and_62 (and_62_out, not_1_out, input_letter[6], input_letter[4], not_6_out, not_7_out);
  and and_63 (and_63_out, not_1_out, input_letter[6], input_letter[4], not_5_out, not_7_out, input_letter[0]);
  and and_64 (and_64_out, not_1_out, input_letter[6], input_letter[4], input_letter[3], not_6_out, not_8_out);
  and and_65 (and_65_out, not_1_out, input_letter[6], input_letter[5], not_4_out, not_5_out, input_letter[2], input_letter[1], input_letter[0]);
  and and_66 (and_66_out, input_letter[7], input_letter[6], input_letter[5], input_letter[4], input_letter[3], input_letter[2], input_letter[1], input_letter[0]);
  and and_67 (and_67_out, not_1_out, input_letter[6], not_3_out, not_5_out, not_6_out, input_letter[0]);
  and and_68 (and_68_out, not_1_out, input_letter[6], not_5_out, not_6_out, not_7_out, input_letter[0]);
  and and_69 (and_69_out, not_1_out, input_letter[6], not_3_out, not_4_out, input_letter[2], input_letter[0]);
  and and_70 (and_70_out, not_1_out, input_letter[6], not_4_out, input_letter[2], not_7_out, input_letter[0]);
  and and_71 (and_71_out, not_1_out, input_letter[6], not_4_out, not_5_out, input_letter[2], input_letter[1]);
  and and_72 (and_72_out, not_1_out, input_letter[6], input_letter[4], not_5_out, not_6_out, not_7_out);
  and and_73 (and_73_out, not_1_out, input_letter[6], input_letter[4], not_5_out, not_6_out, input_letter[0]);
  and and_74 (and_74_out, not_1_out, input_letter[6], input_letter[4], input_letter[3], not_6_out, input_letter[1], not_8_out);
  and and_75 (and_75_out, input_letter[7], input_letter[6], input_letter[5], input_letter[4], input_letter[3], input_letter[2], input_letter[1], input_letter[0]);
  or or_1 (display_letter[7], and_1_out, and_2_out, and_3_out);
  or or_2 (display_letter[6], and_4_out, and_5_out, and_6_out, and_7_out, and_8_out, and_9_out, and_10_out, and_11_out, and_12_out, and_13_out, and_14_out, and_15_out);
  or or_3 (display_letter[5], and_16_out, and_17_out, and_18_out, and_19_out, and_20_out, and_21_out, and_22_out, and_23_out, and_24_out, and_25_out, and_26_out, and_27_out);
  or or_4 (display_letter[4], and_28_out, and_29_out, and_30_out, and_31_out, and_32_out, and_33_out, and_34_out, and_35_out, and_36_out);
  or or_5 (display_letter[3], and_37_out, and_38_out, and_39_out, and_40_out, and_41_out, and_42_out, and_43_out, and_44_out);
  or or_6 (display_letter[2], and_45_out, and_46_out, and_47_out, and_48_out, and_49_out, and_50_out, and_51_out, and_52_out, and_53_out, and_54_out, and_55_out);
  or or_7 (display_letter[1], and_56_out, and_57_out, and_58_out, and_59_out, and_60_out, and_61_out, and_62_out, and_63_out, and_64_out, and_65_out, and_66_out);
  or or_8 (display_letter[0], and_67_out, and_68_out, and_69_out, and_70_out, and_71_out, and_72_out, and_73_out, and_74_out, and_75_out);
endmodule

module byte_saver (
  input  [7:0] current_byte,
  input  byte_received,
  output [7:0] saved_byte
);

  D_Flip_Flop d_ff_1 (.D(current_byte[0]), .clk(byte_received), .Q(saved_byte[0]));  // open: Qn, preset, reset
  D_Flip_Flop d_ff_2 (.D(current_byte[1]), .clk(byte_received), .Q(saved_byte[1]));  // open: Qn, preset, reset
  D_Flip_Flop d_ff_3 (.D(current_byte[2]), .clk(byte_received), .Q(saved_byte[2]));  // open: Qn, preset, reset
  D_Flip_Flop d_ff_4 (.D(current_byte[3]), .clk(byte_received), .Q(saved_byte[3]));  // open: Qn, preset, reset
  D_Flip_Flop d_ff_5 (.D(current_byte[4]), .clk(byte_received), .Q(saved_byte[4]));  // open: Qn, preset, reset
  D_Flip_Flop d_ff_6 (.D(current_byte[5]), .clk(byte_received), .Q(saved_byte[5]));  // open: Qn, preset, reset
  D_Flip_Flop d_ff_7 (.D(current_byte[6]), .clk(byte_received), .Q(saved_byte[6]));  // open: Qn, preset, reset
  D_Flip_Flop d_ff_8 (.D(current_byte[7]), .clk(byte_received), .Q(saved_byte[7]));  // open: Qn, preset, reset
endmodule

module sentence_disp (
  input  [7:0] new_letter,
  input  update,
  output [7:0] seg0,
  output [7:0] seg1,
  output [7:0] seg2,
  output [7:0] seg3,
  output [7:0] seg4,
  output [7:0] seg5
);

  byte_saver byte_saver_1 (.current_byte(new_letter), .byte_received(update), .saved_byte(seg0));
  byte_saver byte_saver_2 (.current_byte(seg0), .byte_received(update), .saved_byte(seg1));
  byte_saver byte_saver_3 (.current_byte(seg1), .byte_received(update), .saved_byte(seg2));
  byte_saver byte_saver_4 (.current_byte(seg2), .byte_received(update), .saved_byte(seg3));
  byte_saver byte_saver_5 (.current_byte(seg3), .byte_received(update), .saved_byte(seg4));
  byte_saver byte_saver_6 (.current_byte(seg4), .byte_received(update), .saved_byte(seg5));
endmodule

// VHDL entity uart_rx, as the project stores it:
--------------------------------------------------------------------------------
-- Project :
-- File    : uart_rx.vhd
-- Author  :
-- Date    :
--
--------------------------------------------------------------------------------
-- Description :
-- UART receiver module for asynchronous serial communication. This version
-- includes improvements for bit timing, stop bit verification, and output signal
-- handling.
--------------------------------------------------------------------------------

LIBRARY ieee;
USE ieee.std_logic_1164.all;
USE ieee.numeric_std.all;

ENTITY uart_rx IS
    PORT (
        i_Clock      : IN  std_logic;                    -- System clock input
        i_RX_Serial  : IN  std_logic;                    -- Serial data input
        o_RX_DV      : OUT std_logic;                    -- Data valid signal
        o_RX_Byte    : OUT std_logic_vector(7 downto 0); -- Output byte
        o_Start_Done : OUT std_logic;                    -- Start bit detected signal
        o_FSM_Mode   : OUT std_logic_vector(2 downto 0);  -- FSM state output for debugging
        o_Bit_Index	 : OUT std_logic_vector(2 downto 0)
    );
END uart_rx;

ARCHITECTURE Behavioral OF uart_rx IS
    type state_type IS (IDLE, RX_START_BIT, RX_DATA_BITS, RX_STOP_BIT, CLEANUP);
    signal r_SM_Main : state_type := IDLE;
    signal r_Start_Done : std_logic := '0';
    signal r_Clock_Count : unsigned(23 downto 0) := (others => '0');
    signal r_Bit_Index : unsigned(2 downto 0) := (others => '0');
    signal r_RX_Byte : std_logic_vector(7 downto 0) := (others => '0');
    signal r_RX_DV : std_logic := '0';
    signal r_FSM_Mode : std_logic_vector(2 downto 0) := (others => '0'); 
    constant N : integer := 3;  -- Number of cycles to confirm bit
    signal bit_counter : integer range 0 to N := 0;  -- N is the number of clock cycles for confirmation
    
    constant CLKS_PER_BIT : integer := 5208;  -- Clock cycles per bit
    
begin
    process(i_Clock)
    begin
        if rising_edge(i_Clock) then            
            case r_SM_Main is
                when IDLE =>
                    r_FSM_Mode <= "001";
                    r_RX_DV <= '0';
                    r_Clock_Count <= (others => '0');
                    r_Bit_Index <= (others => '0');
                    r_Start_Done <= '0';

                    if i_RX_Serial = '0' then
                        bit_counter <= bit_counter + 1;
                        if bit_counter >= N then  -- Confirmed low for N clock cycles
                            r_SM_Main <= RX_START_BIT;
                            bit_counter <= 0;  -- Reset counter
                        end if;
                    else
                        bit_counter <= 0;  -- Reset counter if high is detected
                    end if;

                when RX_START_BIT =>
                    r_FSM_Mode <= "010";
                    r_Clock_Count <= r_Clock_Count + 1;
                    if r_Clock_Count = CLKS_PER_BIT/2 then
                        if i_RX_Serial = '0' then
                            r_Start_Done <= '1';  -- Midpoint confirmation of the start bit
                        else
                            r_Start_Done <= '0';
                        end if;
                    end if;
                    if r_Clock_Count = CLKS_PER_BIT - 1 then
                        r_Clock_Count <= (others => '0');  -- Reset the counter for use in the next state
                        if r_Start_Done = '1' then
                            r_SM_Main <= RX_DATA_BITS;  -- Transition to data bits after confirming start bit
                        else
                            r_SM_Main <= IDLE;  -- Reset if the start bit is not sustained
                        end if;
                    end if;

                when RX_DATA_BITS =>
                    r_FSM_Mode <= "011";
                    r_Clock_Count <= r_Clock_Count + 1;
                    if r_Clock_Count = CLKS_PER_BIT/2 then
                        r_RX_Byte(to_integer(r_Bit_Index)) <= i_RX_Serial;  -- Sample at mid-point
                    end if;
                    if r_Clock_Count = CLKS_PER_BIT - 1 then
                        r_Clock_Count <= (others => '0');    -- Reset for next bit
                        if r_Bit_Index < 7 then
                            r_Bit_Index <= r_Bit_Index + 1;
                        else
                            r_Bit_Index <= (others => '0');
                            r_SM_Main <= RX_STOP_BIT;  -- Proceed to stop bit verification
                        end if;
                    end if;

                when RX_STOP_BIT =>
                    r_FSM_Mode <= "100";
                    r_Clock_Count <= r_Clock_Count + 1;
                    if r_Clock_Count = CLKS_PER_BIT/2 then
                        if i_RX_Serial = '1' then
                            r_RX_DV <= '1';  -- Midpoint confirmation of the stop bit
                        end if;
                    end if;
                    if r_Clock_Count = CLKS_PER_BIT - 1 then
                        r_Clock_Count <= (others => '0');
                        r_SM_Main <= CLEANUP;  -- Cleanup and prepare to return to IDLE
                    end if;

                    -- bit parity

                when CLEANUP =>
                    r_FSM_Mode <= "101";
                    r_SM_Main <= IDLE;
                    r_RX_DV <= '0';

                when others =>
                    r_SM_Main <= IDLE;

            end case;
            o_Bit_Index <= std_logic_vector(r_Bit_Index);
        end if;
    end process;

    o_RX_DV <= r_RX_DV;
    o_RX_Byte <= r_RX_Byte;
    o_Start_Done <= r_Start_Done;
    o_FSM_Mode <= r_FSM_Mode;

END ARCHITECTURE Behavioral;

// VHDL entity clock_tester, as the project stores it:
--------------------------------------------------------------------------------
-- Project :
-- File    :
-- Autor   :
-- Date    :
--
--------------------------------------------------------------------------------
-- Description :
--
--------------------------------------------------------------------------------

LIBRARY ieee;
USE ieee.std_logic_1164.all;
USE ieee.numeric_std.all;

ENTITY clock_tester IS
  PORT (
  ------------------------------------------------------------------------------
  --Insert input ports below
    clock      : IN  std_logic;                    -- input bit example
  ------------------------------------------------------------------------------
  --Insert output ports below
    freq_signal        : OUT std_logic                    -- output bit example
    );
END clock_tester;

--------------------------------------------------------------------------------
--Complete your VHDL description below
--------------------------------------------------------------------------------
ARCHITECTURE TypeArchitecture OF clock_tester IS
    type state_type is (STATE_LOW, STATE_HIGH);
    signal clock_state : state_type := STATE_LOW;  -- Set initial state to STATE_LOW
    signal r_Clock_Test : unsigned(7 downto 0) := (others => '0');
    constant CLKS_PER_BIT : integer := 12500000; --clk freq = 6.25MHz / CLKS_PER_BIT = BR of 1

BEGIN

    process(clock) begin
        if rising_edge(clock) then
            case clock_state is
                when STATE_LOW =>
                    if r_Clock_Test = CLKS_PER_BIT-1 then
                        clock_state <= STATE_HIGH;
                        r_Clock_Test <= (others => '0'); 
                      --  freq_signal <= '1';
                    else
                    	clock_state <= STATE_LOW;
                        	r_Clock_Test <= r_Clock_Test + 1;
                        	freq_signal <= '0';
                    end if;
                when STATE_HIGH =>
                    if r_Clock_Test = CLKS_PER_BIT-1 then
                        clock_state <= STATE_LOW;
                        r_Clock_Test <= (others => '0');
                      --  freq_signal <= '0';
                    else
                    	clock_state <= STATE_HIGH;
                        	r_Clock_Test <= r_Clock_Test + 1;
                        	freq_signal <= '1';
                    end if;
            end case;
        end if;
        
        if clock_state = STATE_LOW then
        	freq_signal <= '0';
        else 
        	freq_signal <= '1';
        end if;
        
    end process;

END TypeArchitecture;

// VHDL entity uart_tx, as the project stores it:
--------------------------------------------------------------------------------
-- Project :
-- uart_rx_log
-- File    :
-- UART_TX
-- Autor   :
-- Selma Benhassine
-- Date    :
 
--
--------------------------------------------------------------------------------
-- Description :
-- The transmitter file for the UART_transmission portion of the project
--
--------------------------------------------------------------------------------

library IEEE;
use IEEE.STD_LOGIC_1164.ALL;
use IEEE.NUMERIC_STD.ALL;

entity uart_tx is
    Port (
        clk_50M : in STD_LOGIC;               -- Input clock, assumed 50 MHz
        data_raw : in STD_LOGIC_VECTOR (7 downto 0);  -- Data byte (8 bits) to transmit
        trigger_raw : in STD_LOGIC;           -- Tells module to begin transmission of data_raw byte
        busy : out STD_LOGIC;                 -- Flag to indicate a transmission is in progress
        serial_out : out STD_LOGIC;            -- UART output serial datastream
        tx_index_out : out STD_LOGIC_VECTOR(3 downto 0) 
    );
end uart_tx;

--------------------------------------------------------------------------------
--Complete your VHDL description below
--------------------------------------------------------------------------------

architecture Behavioral of uart_tx is
	 
	 constant CLKS_PER_BIT: integer := 217;
--  The calculation is as follows:
--
--                                                  1
--     CLKS_PER_BIT =  F_clk [cycles/sec] * --------------------
--                                           baud_rate[bit/sec]
--  so 5208 gives 9.6k baud rate for clk at 50MHz
--  f = 50MHz / 8 when going through logisim
-- last done 217
	 
    type state_type is (STATE_IDLE, STATE_TRANSMITTING, STATE_CLEANUP);
    signal tx_state : state_type := STATE_IDLE;  -- State variable for main finite state machine
    signal data_aug : std_logic_vector(9 downto 0) := (others => '0');  -- Augmented data word to transmit that includes START bit, data byte, and STOP BIT
    signal tx_index : unsigned(3 downto 0) := (others => '0');  -- Index of bit currently transmitting
    signal bit_delay : unsigned(31 downto 0) := (others => '0'); -- Timer to regulate baud rate
   

    signal trigger_0 : std_logic := '0';  -- Synchronizer on trigger input signal
    signal trigger : std_logic := '0';    -- Synchronizer on trigger input signal

    -- Localparam CLKS_PER_BIT is not needed in VHDL since it's used as a constant value in the code directly

begin

    process (clk_50M) begin
        if rising_edge(clk_50M) then
            case tx_state is
                -- Wait for trigger condition indicating it's time to transmit a byte.
                when STATE_IDLE =>
                    busy <= '0';                 -- Indicate that transmitter is idle.
                    serial_out <= '1';           -- Idle output HIGH, per standard UART behavior.
                    if trigger = '1' then        -- Check if received trigger to TX a byte
                        data_aug <= '1' & data_raw & '0';   -- Create augmented byte with start and stop bits
                        busy <= '1';                        -- Indicate that transmitter is busy.
                        bit_delay <= (others => '0');       -- Clear timer used to track duration of each bit
                        tx_index <= (others => '0');        -- Point to first bit of data_aug to TX, namely the start bit
                        tx_state <= STATE_TRANSMITTING;     -- Move on to next state
                    end if;
                    
                -- Transmit all 10 bits with proper the proper duration per bit based on the selected baud rate.
                when STATE_TRANSMITTING =>
                    serial_out <= data_aug(to_integer(tx_index));  -- Set output based on current bit to transmit
                    bit_delay <= bit_delay + 1;                     -- Keep track of duration to hold this bit
                    if bit_delay > to_unsigned(CLKS_PER_BIT, 32) then  -- Check if bit duration has expired
                        if tx_index = "1001" then                  -- Check if just transmitted the final bit, i.e. the STOP bit
                            tx_state <= STATE_CLEANUP;            -- Move on to next state
                        else
                            tx_index <= tx_index + 1;             -- Still more bits to send so, point to next bit
                            bit_delay <= (others => '0');         -- Clear counter used to regulate baud rate
                        end if;
                    end if;
                    
                -- Pause for a few bit durations after full byte transmitted.
                when STATE_CLEANUP =>
                    bit_delay <= bit_delay + 1;                    -- Keep track of how long been in cleanup state
                    if bit_delay > to_unsigned(5 * CLKS_PER_BIT, 32) then  -- If paused HIGH long enough, then return to idle state
                        tx_state <= STATE_IDLE;
                    end if;
                    
                -- Should never get here, but if do, return to IDLE
                when others =>
                    tx_state <= STATE_IDLE;
            end case;
            tx_index_out <= std_logic_vector(tx_index);
        end if;
    end process;

    -- Synchronizer for trigger input
    process (clk_50M) begin
        if rising_edge(clk_50M) then
            trigger_0 <= trigger_raw;
            trigger <= trigger_0;
        end if;
    end process;

end Behavioral;

// VHDL entity uart_tx_tester, as the project stores it:
--------------------------------------------------------------------------------
-- Project : UART_Module
-- File    : UART_Transmitter_Tester
-- Autor   : Selma Benhassine
-- Date    :
--
--------------------------------------------------------------------------------
-- Description : Testbench file for the UART transmitter
--
--------------------------------------------------------------------------------

library IEEE;
use IEEE.STD_LOGIC_1164.ALL;
use IEEE.NUMERIC_STD.ALL;

entity uart_tx_tester is
    Port (
        clk_50M : in STD_LOGIC;               -- Input clock, assumed 50 MHz
        run_test_raw : in STD_LOGIC;          -- HIGH indicates to continuously run test
        tx_busy : in STD_LOGIC;               -- HIGH indicates transmitter is busy 
        data_out : out STD_LOGIC_VECTOR (7 downto 0);  -- Data byte (8 bits) to transmit
        trigger : out STD_LOGIC                -- Trigger to tell UART module to begin transmission
    );
end uart_tx_tester;

architecture Behavioral of uart_tx_tester is

    signal run_test_0 : std_logic := '0';          -- Synchronizer for 'start test' switch input
    signal run_test : std_logic := '0';            -- Synchronizer for 'start test' switch input
    signal tester_state : unsigned(5 downto 0) := (others => '0');  -- FSM state variable
    -- signal byte_index : unsigned(31 downto 0) := unsigned(8*16)-unsigned(1);          -- Pointer to beginning of next byte to transmit in 16 byte message
    constant BYTE_INDEX_INIT: natural := (8*16)-1; -- Calculate the initial value for byte_index
    signal byte_index : unsigned(31 downto 0) := to_unsigned(BYTE_INDEX_INIT, 32); -- Initialize byte_index with the calculated value
	 signal pause_delay : unsigned(31 downto 0) := (others => '0');  -- Counter for delay between re-transmissions of message
    signal trigger_ctr : unsigned(5 downto 0) := (others => '0');    -- Delay to hold trigger high, in clock cycles

    constant STATE_IDLE : unsigned(5 downto 0) := "000000";          -- Legal values for tester_state
    constant STATE_LOAD : unsigned(5 downto 0) := "000010";          -- Legal values for tester_state
    constant STATE_TRIGGER : unsigned(5 downto 0) := "000100";       -- Legal values for tester_state
    constant STATE_POLL_BUSY : unsigned(5 downto 0) := "001000";     -- Legal values for tester_state
    constant STATE_PAUSE : unsigned(5 downto 0) := "010000";         -- Legal values for tester_state

    constant MSG_DELAY : unsigned(31 downto 0) := to_unsigned(100_000, 32);  -- Delay between messages re-transmissions, in clk cycles
	 
	 -- Message to transmit
    signal byte_str : std_logic_vector((8*16)-1 downto 0) := "01001000" & "01100101" & "01101100" & "01101100" & "01101111" & "00100000" & "01010111" & "01101111" &
                                                             "01110010" & "01101100" & "01100100" & "00100001" & "00100000" & "00100000" & "00100000" & "00100000";

-- hello world! is "01001000" & "01100101" & "01101100" & "01101100" & "01101111" & "00100000" & "01010111" & "01101111" &
                                                            -- "01110010" & "01101100" & "01100100" & "00100001" & "00100000" & "00100000" & "00100000" & "00100000";


begin

    -- Synchronizer for "run_test" input since, as tested, this comes from a 
    -- slide switch on the DE10-Lite board, which is not synchronous with the
    -- clock.
    process (clk_50M) begin
        if rising_edge(clk_50M) then
            run_test_0 <= run_test_raw;
            run_test <= run_test_0;
        end if;
    end process;

    -- Main Finite State Machine that sequences the test
    process (clk_50M) begin
        if rising_edge(clk_50M) then
            case tester_state is
                -- Wait for request to begin test.
                when STATE_IDLE =>
                    trigger <= '0';
                    if run_test = '1' then
                        byte_index <= to_unsigned(BYTE_INDEX_INIT, 32);
                        tester_state <= STATE_LOAD;
                    end if;
                    
                -- Output next byte to transmitter module, with trigger still low
                -- so it won't transmit yet.
                when STATE_LOAD =>
                    trigger <= '0';
                    data_out <= byte_str(to_integer(byte_index) downto to_integer(byte_index)-7);
                    trigger_ctr <= to_unsigned(5, 6);
                    tester_state <= STATE_TRIGGER;
                    
                -- Now that previous state output'd the next byte to transmit,
                -- assert the trigger signal to begin the transmission.
                when STATE_TRIGGER =>
                    trigger <= '1';
                    trigger_ctr <= trigger_ctr - 1;
                    if trigger_ctr = 0 then
                        tester_state <= STATE_POLL_BUSY;
                    end if;
                    
                -- Clear trigger signal, and wait until all bits shifted out
                -- for the current byte.
                when STATE_POLL_BUSY =>
                    trigger <= '0';
                    if tx_busy = '0' then
                        if byte_index <= 7 then
                            pause_delay <= (others => '0');
                            tester_state <= STATE_PAUSE;
                        else
                            byte_index <= byte_index - 8;
                            tester_state <= STATE_LOAD;
                        end if;
                    end if;
                    
                -- Once transmitted full message, pause before 
                -- transmitting message again for testing convenience.
                when STATE_PAUSE =>
                    pause_delay <= pause_delay + 1;
                    if pause_delay > to_integer(MSG_DELAY) then
                        tester_state <= STATE_IDLE;
                    end if;
                    
                -- Should never get here, but if do, return to IDLE
                when others =>
                    tester_state <= STATE_IDLE;
            end case;
        end if;
    end process;

end Behavioral;

// VHDL entity divider, as the project stores it:
--------------------------------------------------------------------------------
-- Project :
-- File    :
-- Autor   :
-- Date    :
--
--------------------------------------------------------------------------------
-- Description : dividing clock value to have baud rate down to 50  
--
--------------------------------------------------------------------------------

LIBRARY ieee;
USE ieee.std_logic_1164.all;

ENTITY divider IS
  PORT (
  ------------------------------------------------------------------------------
  --Insert input ports below
    clock      : IN  std_logic;                    -- input bit example
    val        : IN  std_logic_vector(3 DOWNTO 0); -- input vector example
  ------------------------------------------------------------------------------
  --Insert output ports below
    max        : OUT std_logic;                    -- output bit example
    cpt        : OUT std_logic_vector(3 DOWNTO 0)  -- output vector example
    );
END divider;

--------------------------------------------------------------------------------
--Complete your VHDL description below
--------------------------------------------------------------------------------

ARCHITECTURE TypeArchitecture OF divider IS

BEGIN


END TypeArchitecture;
